# Fritzing sketch acelerometro (saved by Fritzing 0.9.0b)

parts:
  Parte1 = Arduino Uno (Rev3)
  Parte2 = Triple Axis Gyro Breakout ITG-3200

nets:
  N1: Parte1.A4/SDA, Parte2.SDA
  N2: Parte1.A5/SCL, Parte2.SCL
  N3: Parte1.D2, Parte2.INT
  5V: Parte1.5V, Parte2.VCC
  GND: Parte1.GND, Parte2.GND
