# Fritzing sketch acelerometro_y_bluetooth (saved by Fritzing 0.9.0b)

parts:
  Parte1 = Arduino Uno (Rev3)
  Parte2 = Triple Axis Gyro Breakout ITG-3200
  Parte3 = Bluetooth Mate Silver

nets:
  N1: Parte1.A4/SDA, Parte2.SDA
  N2: Parte1.A5/SCL, Parte2.SCL
  N3: Parte1.D10_PWM/SS, Parte3.TX_5V
  N4: Parte1.D11_PWM/MOSI, Parte3.RX_5V
  GND: Parte1.GND, Parte2.GND, Parte3.GND
  N5: Parte1.D2, Parte2.INT
  3V3: Parte1.3V3, Parte2.VCC
  5V: Parte1.5V, Parte3.VCC

custom parts:
  Bluetooth Mate Silver: Description: The Bluetooth Mate is very similar to our BlueSMiRF modem, but it is designed specifically to be used with our Arduino Pros and LilyPad Arduinos. These modems work as a serial (RX/TX) pipe, and are a great wireless replacement for serial cables. Any serial stream from 9600 to 115200bps can be passed seamlessly from your computer to your target. Bluetooth Mate has the same pin out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
