# Fritzing sketch bluetooth (saved by Fritzing 0.9.0b)

parts:
  Parte1 = Arduino Uno (Rev3)
  Parte2 = Bluetooth Mate Silver

nets:
  N1: Parte1.D10_PWM/SS, Parte2.TX_5V
  N2: Parte1.D11_PWM/MOSI, Parte2.RX_5V
  GND: Parte1.GND, Parte2.GND
  5V: Parte1.5V, Parte2.VCC
